# Fritzing sketch lcd_verde (saved by Fritzing 0.8.5b)

parts:
  Raspberry_Pi_1 = Raspberry Pi 3
  LCD1 = LCD screen
  R2 = Resistor [tolerance=±5% resistance=2.2k package=THT]
  R3 = Resistor [tolerance=±5% resistance=8.2k package=THT]

nets:
  N1: Raspberry_Pi_1.GIPO11, LCD1.DB7
  N2: Raspberry_Pi_1.GIPO5, LCD1.DB6
  N3: Raspberry_Pi_1.GIPO6, LCD1.DB5
  N4: Raspberry_Pi_1.GIPO13, LCD1.DB4
  N5: Raspberry_Pi_1.GIPO19, LCD1.E
  N6: Raspberry_Pi_1.GIPO26, LCD1.RS
  GND: Raspberry_Pi_1.GND, LCD1.VSS, LCD1.LED-, R2.Pin_0
  N7: Raspberry_Pi_1.5V, R3.Pin_1
  N8: LCD1.V0, R2.Pin_1, R3.Pin_0

notes:
  A 10k potentiometer.
  For blue screen:
  R3=4.7k; R2=1k
